// Logisim project Memory-Project.circ as structural Verilog: 3 circuits, main circuit main
module main (
  input  in_1,
  input  [11:0] in_2,
  input  [11:0] in_3,
  input  in_4
);

  wire clock_1_out;

  Clock clock_1 (.out(clock_1_out));
  _12_bit_Register u_12_bit_register_1 (.D(in_2), .Reset(in_1), .Write(in_4), .C(clock_1_out), .Q(in_3));
endmodule

module _12_bit_Register (
  input  [11:0] D,
  input  Reset,
  input  C,
  input  Write,
  output [11:0] Q
);

  D_Flip_Flop #(.trigger("falling")) d_ff_1 (
    .clk(C), .D(D[0]), .Q(Q[0]), .en(Write), .reset(Reset));  // open: Qn, preset
  D_Flip_Flop #(.trigger("falling")) d_ff_2 (
    .clk(C), .D(D[1]), .Q(Q[1]), .en(Write), .reset(Reset));  // open: Qn, preset
  D_Flip_Flop #(.trigger("falling")) d_ff_3 (
    .clk(C), .D(D[2]), .Q(Q[2]), .en(Write), .reset(Reset));  // open: Qn, preset
  D_Flip_Flop #(.trigger("falling")) d_ff_4 (
    .clk(C), .D(D[3]), .Q(Q[3]), .en(Write), .reset(Reset));  // open: Qn, preset
  D_Flip_Flop #(.trigger("falling")) d_ff_5 (
    .clk(C), .D(D[4]), .Q(Q[4]), .en(Write), .reset(Reset));  // open: Qn, preset
  D_Flip_Flop #(.trigger("falling")) d_ff_6 (
    .clk(C), .D(D[5]), .Q(Q[5]), .en(Write), .reset(Reset));  // open: Qn, preset
  D_Flip_Flop #(.trigger("falling")) d_ff_7 (
    .clk(C), .D(D[6]), .Q(Q[6]), .en(Write), .reset(Reset));  // open: Qn, preset
  D_Flip_Flop #(.trigger("falling")) d_ff_8 (
    .clk(C), .D(D[7]), .Q(Q[7]), .en(Write), .reset(Reset));  // open: Qn, preset
  D_Flip_Flop #(.trigger("falling")) d_ff_9 (
    .clk(C), .D(D[8]), .Q(Q[8]), .en(Write), .reset(Reset));  // open: Qn, preset
  D_Flip_Flop #(.trigger("falling")) d_ff_10 (
    .clk(C), .D(D[9]), .Q(Q[9]), .en(Write), .reset(Reset));  // open: Qn, preset
  D_Flip_Flop #(.trigger("falling")) d_ff_11 (
    .clk(C), .D(D[10]), .Q(Q[10]), .en(Write), .reset(Reset));  // open: Qn, preset
  D_Flip_Flop #(.trigger("falling")) d_ff_12 (
    .clk(C), .D(D[11]), .Q(Q[11]), .en(Write), .reset(Reset));  // open: Qn, preset
endmodule

module Register_File (
  input  [2:0] rs,
  input  [2:0] rt,
  input  [2:0] rd,
  input  [11:0] Data,
  input  C,
  input  Reset,
  input  Write,
  output [11:0] R,
  output [11:0] S
);

  wire demultiplexer_1_out1, demultiplexer_1_out2, demultiplexer_1_out3, demultiplexer_1_out4,
       demultiplexer_1_out5, demultiplexer_1_out6, demultiplexer_1_out7;
  wire [11:0] r0_q, r1_q, r2_q, r3_q, r4_q, r5_q, r6_q, r7_q;

  Demultiplexer #(.select(3), .disabled(0), .enable("false")) demultiplexer_1 (
    .out1(demultiplexer_1_out1), .out2(demultiplexer_1_out2), .out3(demultiplexer_1_out3),
    .out4(demultiplexer_1_out4), .out5(demultiplexer_1_out5), .out6(demultiplexer_1_out6),
    .out7(demultiplexer_1_out7), .in(Write), .sel(rd));  // open: out0
  _12_bit_Register r0 (.D({12{1'b0}}), .Reset(Reset), .C(C), .Q(r0_q));  // open: Write
  _12_bit_Register r1 (.D(Data), .Reset(Reset), .Write(demultiplexer_1_out1), .C(C), .Q(r1_q));
  _12_bit_Register r2 (.D(Data), .Reset(Reset), .Write(demultiplexer_1_out2), .C(C), .Q(r2_q));
  _12_bit_Register r3 (.D(Data), .Reset(Reset), .Write(demultiplexer_1_out3), .C(C), .Q(r3_q));
  _12_bit_Register r4 (.D(Data), .Reset(Reset), .Write(demultiplexer_1_out4), .C(C), .Q(r4_q));
  _12_bit_Register r5 (.D(Data), .Reset(Reset), .Write(demultiplexer_1_out5), .C(C), .Q(r5_q));
  _12_bit_Register r6 (.D(Data), .Reset(Reset), .Write(demultiplexer_1_out6), .C(C), .Q(r6_q));
  _12_bit_Register r7 (.D(Data), .Reset(Reset), .Write(demultiplexer_1_out7), .C(C), .Q(r7_q));
  Multiplexer #(.select(3), .width(12), .enable("false")) multiplexer_1 (
    .in0(r0_q), .in1(r1_q), .in2(r2_q), .in3(r3_q), .in4(r4_q), .in5(r5_q), .in6(r6_q), .in7(r7_q), .out(R),
    .sel(rs));
  Multiplexer #(.select(3), .width(12), .enable("false")) multiplexer_2 (
    .in0(r0_q), .in1(r1_q), .in2(r2_q), .in3(r3_q), .in4(r4_q), .in5(r5_q), .in6(r6_q), .in7(r7_q), .out(S),
    .sel(rt));
endmodule
